# Fritzing sketch LittleBuddy (saved by Fritzing 0.9.4)

parts:
  RFM69 = RFM69W
  ANT1 = Antenna
  M1 = STM32F103C8T6 blue mini board

nets:
  reset radio: RFM69.RESET, M1.B5
  callback: RFM69.DIO0, M1.B4
  aux. status: RFM69.DIO4, M1.B3
  3.3V/radio power: RFM69.3V3, M1.3.3V, M1.3.3
  GND: RFM69.GND, M1.G, M1.GND
  N1: RFM69.ANA, ANT1.antenna_lead
  SCK: RFM69.SCK, M1.A5
  MISO: RFM69.MISO, M1.A6
  MOSI: RFM69.MOSI, M1.A7
  NSS: RFM69.NSS, M1.A4

notes:
  Currently,
  DIO 4 [aux. status]
  is unused, but can provide extra information about transmission if needed. (It also provides extra support for the radio chip on top of the STM32)
